// Logisim project LC-2200-16.circ as structural Verilog: 5 circuits, main circuit main
module main (
);


  // Notes on the sheet:
  //   FALL 2015
endmodule

module datapath (
);

  wire ALUHi, ALULo, CLK, DrALU, DrMEM, DrOFF, DrPC, DrREG, LdA, LdB, LdIR, LdMAR, LdPC, LdZ, not_1_out,
       not_2_out, or_1_out, RegSelHi, RegSelLo, WrMEM, WrREG, Z;
  wire [3:0] controlled_buffer_1_out, controlled_buffer_1_out_2, controlled_buffer_1_out_3,
       controlled_buffer_1_out_4, SEL_REG;
  wire [15:0] A_q, alu_1_out, B_q, bit_extender_1_out, IR, MAR_q, PC_q, ram_1_data, register_file_1_out;

  Clock CLOCK (.out(CLK));
  assign {controlled_buffer_1_out_4, controlled_buffer_1_out_3, controlled_buffer_1_out_2, controlled_buffer_1_out} = DrPC ? PC_q : 16'bz;  // Controlled_Buffer controlled_buffer_1
  Register #(.width(16)) PC (
    .D({controlled_buffer_1_out_4, controlled_buffer_1_out_3, controlled_buffer_1_out_2, controlled_buffer_1_out}),
    .en(LdPC), .Q(PC_q), .clk(CLK));  // open: clr
  or or_1 (or_1_out, controlled_buffer_1_out_4[3], controlled_buffer_1_out_4[2], controlled_buffer_1_out_4[1], controlled_buffer_1_out_4[0], controlled_buffer_1_out_3[3], controlled_buffer_1_out_3[2], controlled_buffer_1_out_3[1], controlled_buffer_1_out_3[0], controlled_buffer_1_out_2[3], controlled_buffer_1_out_2[2], controlled_buffer_1_out_2[1], controlled_buffer_1_out_2[0], controlled_buffer_1_out[3], controlled_buffer_1_out[2], controlled_buffer_1_out[1], controlled_buffer_1_out[0]);
  not not_1 (not_1_out, or_1_out);
  microcontroller microcontroller_1 (
    .IR(IR), .Z(Z), .CLK(CLK),
    .STATE({DrALU, DrMEM, DrOFF, DrPC, DrREG, LdA, LdB, LdIR, LdMAR, LdPC, LdZ, WrREG, WrMEM, RegSelLo, RegSelHi, ALULo, ALUHi}));
  Register #(.width(16)) A (
    .D({controlled_buffer_1_out_4, controlled_buffer_1_out_3, controlled_buffer_1_out_2, controlled_buffer_1_out}),
    .en(LdA), .Q(A_q), .clk(CLK));  // open: clr
  Register #(.width(1)) u_Z (.D(not_1_out), .en(LdZ), .Q(Z), .clk(CLK));  // open: clr
  ALU alu_1 (.op({ALUHi, ALULo}), .A(A_q), .B(B_q), .OUT(alu_1_out));
  Register #(.width(16)) B (
    .D({controlled_buffer_1_out_4, controlled_buffer_1_out_3, controlled_buffer_1_out_2, controlled_buffer_1_out}),
    .en(LdB), .Q(B_q), .clk(CLK));  // open: clr
  assign {controlled_buffer_1_out_4, controlled_buffer_1_out_3, controlled_buffer_1_out_2, controlled_buffer_1_out} = DrALU ? alu_1_out : 16'bz;  // Controlled_Buffer controlled_buffer_2
  register_file register_file_1 (
    .IN({controlled_buffer_1_out_4, controlled_buffer_1_out_3, controlled_buffer_1_out_2, controlled_buffer_1_out}),
    .SEL_REG(SEL_REG), .WrREG(WrREG), .CLK(CLK), .OUT(register_file_1_out));
  assign {controlled_buffer_1_out_4, controlled_buffer_1_out_3, controlled_buffer_1_out_2, controlled_buffer_1_out} = DrREG ? register_file_1_out : 16'bz;  // Controlled_Buffer controlled_buffer_3
  Multiplexer #(.select(2), .width(4)) multiplexer_1 (
    .in0(IR[12:9]), .in1(IR[8:5]), .in2(IR[4:1]), .out(SEL_REG), .sel({RegSelHi, RegSelLo}));  // open: in3, en
  Register #(.width(16)) MAR (
    .D({controlled_buffer_1_out_4, controlled_buffer_1_out_3, controlled_buffer_1_out_2, controlled_buffer_1_out}),
    .en(LdMAR), .Q(MAR_q), .clk(CLK));  // open: clr
  RAM #(.addrWidth(16), .dataWidth(16)) ram_1 (
    .addr(MAR_q), .data(ram_1_data), .clk(CLK), .ld(not_2_out));  // open: sel, clr
  not not_2 (not_2_out, WrMEM);
  assign ram_1_data = WrMEM ? {controlled_buffer_1_out_4, controlled_buffer_1_out_3, controlled_buffer_1_out_2, controlled_buffer_1_out} : 16'bz;  // Controlled_Buffer controlled_buffer_4
  assign {controlled_buffer_1_out_4, controlled_buffer_1_out_3, controlled_buffer_1_out_2, controlled_buffer_1_out} = DrMEM ? ram_1_data : 16'bz;  // Controlled_Buffer controlled_buffer_5
  Register #(.width(16)) u_IR (
    .D({controlled_buffer_1_out_4, controlled_buffer_1_out_3, controlled_buffer_1_out_2, controlled_buffer_1_out}),
    .en(LdIR), .Q(IR), .clk(CLK));  // open: clr
  assign bit_extender_1_out = {{11{IR[4]}}, IR[4:0]};  // Bit_Extender bit_extender_1
  assign {controlled_buffer_1_out_4, controlled_buffer_1_out_3, controlled_buffer_1_out_2, controlled_buffer_1_out} = DrOFF ? bit_extender_1_out : 16'bz;  // Controlled_Buffer controlled_buffer_6
  Hex_Digit_Display hex_digit_display_1 (.value(controlled_buffer_1_out_4));  // open: dp
  Hex_Digit_Display hex_digit_display_2 (.value(controlled_buffer_1_out_3));  // open: dp
  Hex_Digit_Display hex_digit_display_3 (.value(controlled_buffer_1_out_2));  // open: dp
  Hex_Digit_Display hex_digit_display_4 (.value(controlled_buffer_1_out));  // open: dp

  // Other names for the same wires on the sheet: OPCODE[2:0] = IR[15:13]; RX[3:0] = IR[12:9]; RY[3:0] = IR[8:5];
  //   RZ[3:0] = IR[4:1]
endmodule

module ALU (
  input  [15:0] A,
  input  [15:0] B,
  input  [1:0] op,
  output [15:0] OUT
);

  wire [15:0] A_plus_plus, ADD, NAND, SUB;

  Adder #(.width(16)) adder_1 (.a(A), .b(B), .out(ADD));  // open: cin, cout
  Subtractor #(.width(16)) subtractor_1 (.a(A), .b(B), .out(SUB));  // open: bin, bout
  assign NAND = ~(A & B);  // NAND_Gate nand_1, 16 bits wide
  Adder #(.width(16)) adder_2 (.a(A), .b(16'h1), .out(A_plus_plus));  // open: cin, cout
  Multiplexer #(.select(2), .width(16)) multiplexer_1 (
    .in0(ADD), .in1(NAND), .in2(SUB), .in3(A_plus_plus), .out(OUT), .sel(op));  // open: en

  // Notes on the sheet:
  //   00-ADD
  //   01-NAND
  //   10-SUB
  //   11-A++
endmodule

module register_file (
  input  [15:0] IN,
  input  [3:0] SEL_REG,
  input  CLK,
  input  WrREG,
  output [15:0] OUT
);

  wire and_1_out, and_2_out, and_3_out, and_4_out, and_5_out, and_6_out, and_7_out, and_8_out, and_9_out,
       and_10_out, and_11_out, and_12_out, and_13_out, and_14_out, and_15_out, reg_0, reg_1, reg_2, reg_3,
       reg_4, reg_5, reg_6, reg_7, reg_8, reg_9, reg_10, reg_11, reg_12, reg_13, reg_14, reg_15;
  wire [15:0] OUT_1, OUT_2, OUT_3, OUT_4, OUT_5, OUT_6, OUT_7, OUT_8, OUT_9, OUT_10, OUT_11, OUT_12, OUT_13,
       OUT_14, OUT_15;

  Decoder #(.select(4)) decoder_1 (
    .out0(reg_0), .out1(reg_1), .out2(reg_2), .out3(reg_3), .out4(reg_4), .out5(reg_5), .out6(reg_6),
    .out7(reg_7), .out8(reg_8), .out9(reg_9), .out10(reg_10), .out11(reg_11), .out12(reg_12), .out13(reg_13),
    .out14(reg_14), .out15(reg_15), .sel(SEL_REG));  // open: en
  Register #(.width(16)) register_1 (.D(IN), .en(and_1_out), .Q(OUT_1), .clk(CLK));  // open: clr
  and and_1 (and_1_out, reg_1, WrREG);
  Register #(.width(16)) register_2 (.D(IN), .en(and_2_out), .Q(OUT_2), .clk(CLK));  // open: clr
  and and_2 (and_2_out, reg_2, WrREG);
  Register #(.width(16)) register_3 (.D(IN), .en(and_3_out), .Q(OUT_3), .clk(CLK));  // open: clr
  and and_3 (and_3_out, reg_3, WrREG);
  and and_4 (and_4_out, reg_4, WrREG);
  and and_5 (and_5_out, reg_5, WrREG);
  and and_6 (and_6_out, reg_6, WrREG);
  and and_7 (and_7_out, reg_7, WrREG);
  Register #(.width(16)) register_4 (.D(IN), .en(and_4_out), .Q(OUT_4), .clk(CLK));  // open: clr
  Register #(.width(16)) register_5 (.D(IN), .en(and_5_out), .Q(OUT_5), .clk(CLK));  // open: clr
  Register #(.width(16)) register_6 (.D(IN), .en(and_6_out), .Q(OUT_6), .clk(CLK));  // open: clr
  Register #(.width(16)) register_7 (.D(IN), .en(and_7_out), .Q(OUT_7), .clk(CLK));  // open: clr
  Multiplexer #(.select(4), .width(16)) multiplexer_1 (
    .in0({16{1'b0}}), .in1(OUT_1), .in2(OUT_2), .in3(OUT_3), .in4(OUT_4), .in5(OUT_5), .in6(OUT_6),
    .in7(OUT_7), .in8(OUT_8), .in9(OUT_9), .in10(OUT_10), .in11(OUT_11), .in12(OUT_12), .in13(OUT_13),
    .in14(OUT_14), .in15(OUT_15), .out(OUT), .sel(SEL_REG));  // open: en
  and and_8 (and_8_out, reg_8, WrREG);
  and and_9 (and_9_out, reg_9, WrREG);
  and and_10 (and_10_out, reg_10, WrREG);
  and and_11 (and_11_out, reg_11, WrREG);
  Register #(.width(16)) register_8 (.D(IN), .en(and_8_out), .Q(OUT_8), .clk(CLK));  // open: clr
  Register #(.width(16)) register_9 (.D(IN), .en(and_9_out), .Q(OUT_9), .clk(CLK));  // open: clr
  Register #(.width(16)) register_10 (.D(IN), .en(and_10_out), .Q(OUT_10), .clk(CLK));  // open: clr
  Register #(.width(16)) register_11 (.D(IN), .en(and_11_out), .Q(OUT_11), .clk(CLK));  // open: clr
  Register #(.width(16)) register_12 (.D(IN), .en(and_12_out), .Q(OUT_12), .clk(CLK));  // open: clr
  and and_12 (and_12_out, reg_12, WrREG);
  Register #(.width(16)) register_13 (.D(IN), .en(and_13_out), .Q(OUT_13), .clk(CLK));  // open: clr
  and and_13 (and_13_out, reg_13, WrREG);
  Register #(.width(16)) register_14 (.D(IN), .en(and_14_out), .Q(OUT_14), .clk(CLK));  // open: clr
  and and_14 (and_14_out, reg_14, WrREG);
  Register #(.width(16)) register_15 (.D(IN), .en(and_15_out), .Q(OUT_15), .clk(CLK));  // open: clr
  and and_15 (and_15_out, reg_15, WrREG);

  // Other names for the same wires on the sheet: SEL[3:0] = SEL_REG

  // Notes on the sheet:
  //   REGISTER 0 is always 0
endmodule

module microcontroller (
  input  [15:0] IR,
  input  Z,
  input  CLK,
  output [16:0] STATE
);

  wire chkZ, OPTest;
  wire [5:0] branch_state, multiplexer_1_out, next_state, opcode_to_state, register_1_q;

  ROM #(.addrWidth(6), .dataWidth(25)) rom_1 (
    .addr(register_1_q), .data({next_state, STATE, OPTest, chkZ}));  // open: sel
  Register #(.width(6)) register_1 (.D(multiplexer_1_out), .en(1'b1), .Q(register_1_q), .clk(CLK));  // open: clr
  Multiplexer #(.select(2), .width(6), .enable("false")) multiplexer_1 (
    .in0(next_state), .in1(opcode_to_state), .in2(branch_state), .out(multiplexer_1_out), .sel({chkZ, OPTest}));  // open: in3
  ROM #(.addrWidth(3), .dataWidth(6)) rom_2 (.addr(IR[15:13]), .data(opcode_to_state));  // open: sel
  ROM #(.addrWidth(2), .dataWidth(6)) rom_3 (.addr({1'b0, Z}), .data(branch_state));  // open: sel

  // Other names for the same wires on the sheet: state_t[24:0] = {next_state, STATE, OPTest, chkZ};
  //   OUT_SIGNALS[16:0] = STATE

  // Notes on the sheet:
  //   contents of rom_1 (hex, n*v repeats v):
  //   8a400 120800 4020e 206020 285010 40080 386020 405010 40088 506020 591000 40080 686020 711000 7c0400
  //   20080 886020 911000 9c0400 4040 a86000 b05020 bc0104 1 c8a000 d11000 40200 e080a0 4200 e80000
  //   contents of rom_2 (hex, n*v repeats v):
  //   3 6 9 c 10 14 1b 1d
  //   contents of rom_3 (hex, n*v repeats v):
  //   0 18
endmodule
