// Logisim project LC-2200-32.circ as structural Verilog: 8 circuits, main circuit Processor
module Processor (
);

  wire Clock, Clr, DrALU, DrMEM, DrOFF, DrPC, DrReg, INT_ACK, LdA, LdB, LdIR, LdMAR, LdPC, LdZ, not_1_out,
       WrMEM, WrREG, Z, ZeroDetectOut;
  wire [1:0] FUNC, RegSel;
  wire [3:0] IR_q, IR_q_2, IR_q_3, Opcode, Reg_num;
  wire [19:4] IR_q_4;
  wire [23:0] MAR_q;
  wire [31:0] A_q, B_q, controlled_buffer_1_out, ensure_above_0x10_1_out, PC_q, ram_1_data,
       registers_1_data_out, ZeroDetect;

  Register #(.width(32)) PC (.D(controlled_buffer_1_out), .en(LdPC), .Q(PC_q), .clk(Clock), .clr(Clr));
  ensure_above_0x10 ensure_above_0x10_1 (.IN(PC_q), .OUT(ensure_above_0x10_1_out));
  assign controlled_buffer_1_out = DrPC ? ensure_above_0x10_1_out : 32'bz;  // Controlled_Buffer controlled_buffer_1
  State_Machine state_machine_1 (
    .Clock(Clock), .OpCode(Opcode), .Z(Z), .DrREG(DrReg), .DrMEM(DrMEM), .DrALU(DrALU), .DrPC(DrPC),
    .DrOFF(DrOFF), .LdPC(LdPC), .LdIR(LdIR), .LdMAR(LdMAR), .LdA(LdA), .LdB(LdB), .LdZ(LdZ), .WrREG(WrREG),
    .WrMEM(WrMEM), .RegSel(RegSel), .ALU_FUNC(FUNC), .INT_ACK(INT_ACK), .ADDR_BUS(controlled_buffer_1_out),
    .DATA_BUS(controlled_buffer_1_out));
  Register #(.width(32)) A (.D(controlled_buffer_1_out), .en(LdA), .Q(A_q), .clk(Clock), .clr(Clr));
  ALU alu_1 (.FUNC(FUNC), .INPUT_A(A_q), .INPUT_B(B_q), .out_4(ZeroDetect));
  Register #(.width(32)) B (.D(controlled_buffer_1_out), .en(LdB), .Q(B_q), .clk(Clock), .clr(Clr));
  assign controlled_buffer_1_out = DrALU ? ZeroDetect : 32'bz;  // Controlled_Buffer controlled_buffer_2
  Registers registers_1 (
    .WrReg(WrREG), .RegSel(Reg_num), .Data_In(controlled_buffer_1_out), .Clock(Clock), .ClearRegFile(Clr),
    .Data_Out(registers_1_data_out));
  assign controlled_buffer_1_out = DrReg ? registers_1_data_out : 32'bz;  // Controlled_Buffer controlled_buffer_3
  Clock clock_1 (.out(Clock));
  Button button_1 (.out(Clr));
  Register #(.width(24)) MAR (.D(controlled_buffer_1_out[23:0]), .en(LdMAR), .Q(MAR_q), .clk(Clock), .clr(Clr));
  not not_1 (not_1_out, WrMEM);
  RAM #(.addrWidth(24), .dataWidth(32), .bus("separate")) ram_1 (
    .addr(MAR_q), .din(controlled_buffer_1_out), .data(ram_1_data), .str(WrMEM), .clk(Clock), .ld(not_1_out),
    .clr(Clr));  // open: sel
  assign controlled_buffer_1_out = DrMEM ? ram_1_data : 32'bz;  // Controlled_Buffer controlled_buffer_4
  Register #(.width(32)) IR (
    .D(controlled_buffer_1_out), .en(LdIR), .Q({Opcode, IR_q_2, IR_q, IR_q_4, IR_q_3}), .clk(Clock), .clr(Clr));
  Multiplexer #(.select(2), .width(4), .enable("false")) multiplexer_1 (
    .in0(IR_q_2), .in1(IR_q), .in2(IR_q_3), .in3(4'b1100), .out(Reg_num), .sel(RegSel));
  assign controlled_buffer_1_out = DrOFF ? {{13{IR_q_4[19]}}, IR_q_4[18:4], IR_q_3} : 32'bz;  // Controlled_Buffer controlled_buffer_5
  Comparator #(.width(32), .mode("unsigned")) comparator_1 (
    .a(ZeroDetect), .b({32{1'b0}}), .eq(ZeroDetectOut));  // open: gt, lt
  Register #(.width(1)) Z_Register (.D(ZeroDetectOut), .en(LdZ), .Q(Z), .clk(Clock), .clr(Clr));

  // Notes on the sheet:
  //   00 = RX
  //   01 = RY
  //   10 = RZ
  //   $k0
endmodule

module ALU (
  input  [31:0] INPUT_A,
  input  [31:0] INPUT_B,
  input  [1:0] FUNC,
  output [31:0] out_4
);

  wire [31:0] adder_1_out, adder_2_out, nand_1_out, subtractor_1_out;

  Adder #(.width(32)) adder_1 (.a(INPUT_A), .b(INPUT_B), .out(adder_1_out));  // open: cin, cout
  assign nand_1_out = ~(INPUT_A & INPUT_B);  // NAND_Gate nand_1, 32 bits wide
  Multiplexer #(.select(2), .width(32), .enable("false")) multiplexer_1 (
    .in0(adder_1_out), .in1(nand_1_out), .in2(subtractor_1_out), .in3(adder_2_out), .out(out_4), .sel(FUNC));
  Subtractor #(.width(32)) subtractor_1 (.a(INPUT_A), .b(INPUT_B), .out(subtractor_1_out));  // open: bin, bout
  Adder #(.width(32)) adder_2 (.a(INPUT_A), .b(32'h1), .out(adder_2_out));  // open: cin, cout
endmodule

module State_Machine (
  input  Clock,
  input  [3:0] OpCode,
  input  Z,
  output DrREG,
  output DrMEM,
  output DrALU,
  output DrPC,
  output DrOFF,
  output LdPC,
  output LdIR,
  output LdMAR,
  output LdA,
  output LdB,
  output LdZ,
  output WrREG,
  output WrMEM,
  output [1:0] RegSel,
  output [1:0] ALU_FUNC,
  output INT_ACK,
  output [31:0] ADDR_BUS,
  output [31:0] DATA_BUS
);

  wire chkInt, chkZ, DrEnI, DrIntData, IE, intergenerator_1_int_ack_out, intergenerator_1_intout, Ipending,
       LdEnInt, OnInt, OpTest;
  wire [1:0] or_1_out, rom_1_data_2;
  wire [3:0] rom_1_data;
  wire [5:0] multiplexer_1_out, register_1_q, rom_2_data, rom_3_data, rom_4_data;
  wire [31:0] keyboard_1_data, PendingData_q;

  Register #(.width(1)) u_IE (.D(DrEnI), .en(LdEnInt), .Q(IE), .clk(Clock));  // open: clr
  Hex_Digit_Display hex_digit_display_1 (.value({2'b00, rom_1_data_2}));  // open: dp
  and and_1 (OnInt, IE, Ipending);
  Intergenerator intergenerator_1 (
    .IntOut(intergenerator_1_intout), .CLK(Clock), .INT_ACK(INT_ACK), .INT_BUS(ADDR_BUS),
    .INT_ACK_OUT(intergenerator_1_int_ack_out));
  Register #(.width(6)) register_1 (.D(multiplexer_1_out), .en(Clock), .Q(register_1_q), .clk(Clock));  // open: clr
  Hex_Digit_Display hex_digit_display_2 (.value(rom_1_data));  // open: dp
  keyboard keyboard_1 (
    .INT_ACK(intergenerator_1_int_ack_out), .CLK(Clock), .ADDR_BUS(ADDR_BUS), .DATA(keyboard_1_data),
    .INT(intergenerator_1_intout));
  Multiplexer #(.select(2), .width(6), .enable("false")) multiplexer_1 (
    .in0({rom_1_data_2, rom_1_data}), .in1(rom_2_data), .in2(rom_3_data), .in3(rom_4_data),
    .out(multiplexer_1_out), .sel(or_1_out));
  assign or_1_out = {chkZ, OpTest} | {2{chkInt}};  // OR_Gate or_1, 2 bits wide
  ROM #(.addrWidth(6), .dataWidth(30)) rom_1 (
    .addr(register_1_q),
    .data({DrIntData, chkZ, OpTest, ALU_FUNC, RegSel, WrMEM, WrREG, LdZ, LdB, LdA, LdMAR, LdIR, LdPC, DrOFF, DrPC, DrALU, DrMEM, DrREG, rom_1_data_2, rom_1_data, DrEnI, LdEnInt, INT_ACK, chkInt}));  // open: sel
  Register #(.width(32)) PendingData (.D(keyboard_1_data), .en(INT_ACK), .Q(PendingData_q), .clk(Clock));  // open: clr
  Register #(.width(1)) register_2 (
    .D(intergenerator_1_intout), .en(intergenerator_1_intout), .Q(Ipending), .clk(Clock), .clr(INT_ACK));
  assign DATA_BUS = DrIntData ? PendingData_q : 32'bz;  // Controlled_Buffer controlled_buffer_1
  ROM #(.addrWidth(4), .dataWidth(6)) rom_2 (.addr(OpCode), .data(rom_2_data));  // open: sel
  ROM #(.addrWidth(2), .dataWidth(6)) rom_3 (.addr({1'b0, Z}), .data(rom_3_data));  // open: sel
  ROM #(.addrWidth(2), .dataWidth(6)) rom_4 (.addr({1'b0, OnInt}), .data(rom_4_data));  // open: sel

  // Notes on the sheet:
  //   ADDR_BUS
  //   INT
  //   contents of rom_1 (hex, n*v repeats v):
  //   62011 10820 e009000 840440 1080450 201000 840470 1080480 2201000 8404a0 840b0 201000 8404d0 840e0
  //   210f0 200800 840510 84120 21130 400400 40550 880560 4101170 10000000 42190 841a0 9000 a021c0 8400
  //   1d0 1a021f4 20202 8800 c 4 180840c 40650 880660 21270 20400000
  //   contents of rom_2 (hex, n*v repeats v):
  //   3 6 9 c 10 14 1b 1d 1d 1d 21 22 23 1d 24
  //   contents of rom_3 (hex, n*v repeats v):
  //   0 18
  //   contents of rom_4 (hex, n*v repeats v):
  //   1 1e
endmodule

// 0?
module Zero_Detection (
  input  [31:0] In,
  output Out
);

  Comparator #(.width(32), .mode("unsigned")) comparator_1 (.a(In), .b({32{1'b0}}), .eq(Out));  // open: gt, lt
endmodule

// Reg File
module Registers (
  input  [31:0] Data_In,
  input  WrReg,
  input  [3:0] RegSel,
  input  Clock,
  input  ClearRegFile,
  output [31:0] Data_Out
);

  wire and_1_out, and_2_out, and_3_out, and_4_out, and_5_out, and_6_out, and_7_out, and_8_out, and_9_out,
       and_10_out, and_11_out, and_12_out, and_13_out, and_14_out, and_15_out, and_16_out, decoder_1_out0,
       decoder_1_out1, decoder_1_out2, decoder_1_out3, decoder_1_out4, decoder_1_out5, decoder_1_out6,
       decoder_1_out7, decoder_1_out8, decoder_1_out9, decoder_1_out10, decoder_1_out11, decoder_1_out12,
       decoder_1_out13, decoder_1_out14, decoder_1_out15;
  wire [31:0] a0, a1, a2, at, k0, pr, ra, s0, s1, s2, sp, t0, t1, t2, v0, zero;

  Decoder #(.select(4), .enable("false")) decoder_1 (
    .out0(decoder_1_out0), .out1(decoder_1_out1), .out2(decoder_1_out2), .out3(decoder_1_out3),
    .out4(decoder_1_out4), .out5(decoder_1_out5), .out6(decoder_1_out6), .out7(decoder_1_out7),
    .out8(decoder_1_out8), .out9(decoder_1_out9), .out10(decoder_1_out10), .out11(decoder_1_out11),
    .out12(decoder_1_out12), .out13(decoder_1_out13), .out14(decoder_1_out14), .out15(decoder_1_out15),
    .sel(RegSel));
  and and_1 (and_1_out, decoder_1_out0, WrReg);
  and and_2 (and_2_out, decoder_1_out1, WrReg);
  and and_3 (and_3_out, decoder_1_out2, WrReg);
  and and_4 (and_4_out, decoder_1_out3, WrReg);
  and and_5 (and_5_out, decoder_1_out4, WrReg);
  and and_6 (and_6_out, decoder_1_out5, WrReg);
  and and_7 (and_7_out, decoder_1_out6, WrReg);
  and and_8 (and_8_out, decoder_1_out7, WrReg);
  and and_9 (and_9_out, decoder_1_out8, WrReg);
  and and_10 (and_10_out, decoder_1_out9, WrReg);
  and and_11 (and_11_out, decoder_1_out10, WrReg);
  and and_12 (and_12_out, decoder_1_out11, WrReg);
  and and_13 (and_13_out, decoder_1_out12, WrReg);
  and and_14 (and_14_out, decoder_1_out13, WrReg);
  and and_15 (and_15_out, decoder_1_out14, WrReg);
  and and_16 (and_16_out, decoder_1_out15, WrReg);
  Register #(.width(32)) u_zero (.D(Data_In), .en(and_1_out), .Q(zero), .clk(Clock), .clr(1'b1));
  Register #(.width(32)) u_at (.D(Data_In), .en(and_2_out), .Q(at), .clk(Clock), .clr(ClearRegFile));
  Register #(.width(32)) u_v0 (.D(Data_In), .en(and_3_out), .Q(v0), .clk(Clock), .clr(ClearRegFile));
  Register #(.width(32)) u_a0 (.D(Data_In), .en(and_4_out), .Q(a0), .clk(Clock), .clr(ClearRegFile));
  Register #(.width(32)) u_a1 (.D(Data_In), .en(and_5_out), .Q(a1), .clk(Clock), .clr(ClearRegFile));
  Register #(.width(32)) u_a2 (.D(Data_In), .en(and_6_out), .Q(a2), .clk(Clock), .clr(ClearRegFile));
  Register #(.width(32)) u_t0 (.D(Data_In), .en(and_7_out), .Q(t0), .clk(Clock), .clr(ClearRegFile));
  Register #(.width(32)) u_t1 (.D(Data_In), .en(and_8_out), .Q(t1), .clk(Clock), .clr(ClearRegFile));
  Register #(.width(32)) u_t2 (.D(Data_In), .en(and_9_out), .Q(t2), .clk(Clock), .clr(ClearRegFile));
  Register #(.width(32)) u_s0 (.D(Data_In), .en(and_10_out), .Q(s0), .clk(Clock), .clr(ClearRegFile));
  Register #(.width(32)) u_s1 (.D(Data_In), .en(and_11_out), .Q(s1), .clk(Clock), .clr(ClearRegFile));
  Register #(.width(32)) u_s2 (.D(Data_In), .en(and_12_out), .Q(s2), .clk(Clock), .clr(ClearRegFile));
  Register #(.width(32)) u_k0 (.D(Data_In), .en(and_13_out), .Q(k0), .clk(Clock), .clr(ClearRegFile));
  Register #(.width(32)) u_sp (.D(Data_In), .en(and_14_out), .Q(sp), .clk(Clock), .clr(ClearRegFile));
  Register #(.width(32)) u_pr (.D(Data_In), .en(and_15_out), .Q(pr), .clk(Clock), .clr(ClearRegFile));
  Register #(.width(32)) u_ra (.D(Data_In), .en(and_16_out), .Q(ra), .clk(Clock), .clr(ClearRegFile));
  Multiplexer #(.select(4), .width(32), .enable("false")) multiplexer_1 (
    .in0(zero), .in1(at), .in2(v0), .in3(a0), .in4(a1), .in5(a2), .in6(t0), .in7(t1), .in8(t2), .in9(s0),
    .in10(s1), .in11(s2), .in12(k0), .in13(sp), .in14(pr), .in15(ra), .out(Data_Out), .sel(RegSel));

  // Other names for the same wires on the sheet: Din[31:0] = Data_In; en = WrReg
endmodule

module Intergenerator (
  input  CLK,
  input  INT_ACK,
  output IntOut,
  output INT_ACK_OUT,
  output [31:0] INT_BUS
);

  wire INT_PENDING, not_1_out, register_3_q, SEND_INT_VEC, wait_for_ack;
  wire [10:0] adder_1_out, register_2_q;

  and and_1 (SEND_INT_VEC, INT_ACK, INT_PENDING);
  Register #(.width(1)) register_1 (.D(wait_for_ack), .en(wait_for_ack), .Q(INT_PENDING), .clk(CLK));  // open: clr
  Adder #(.width(11)) adder_1 (.a(11'h1), .b(register_2_q), .out(adder_1_out));  // open: cin, cout
  not not_1 (not_1_out, SEND_INT_VEC);
  Register #(.width(11)) register_2 (.D(adder_1_out), .en(1'b1), .Q(register_2_q), .clk(CLK), .clr(register_3_q));
  and and_2 (INT_ACK_OUT, INT_ACK, not_1_out);
  Comparator #(.width(11), .mode("unsigned")) comparator_1 (
    .a(11'h400), .b(register_2_q), .eq(wait_for_ack));  // open: gt, lt
  assign IntOut = wait_for_ack ? 1'b1 : 1'bz;  // Controlled_Buffer controlled_buffer_1
  Register #(.width(1)) register_3 (.D(wait_for_ack), .en(1'b1), .Q(register_3_q), .clk(CLK), .clr(register_3_q));
  assign INT_BUS = SEND_INT_VEC ? 32'h1 : 32'bz;  // Controlled_Buffer controlled_buffer_2
endmodule

module ensure_above_0x10 (
  input  [31:0] IN,
  output [31:0] OUT
);

  wire comparator_1_lt;

  Comparator #(.width(32)) comparator_1 (.a(IN), .b(32'h10), .lt(comparator_1_lt));  // open: gt, eq
  Multiplexer #(.width(32), .enable("false")) multiplexer_1 (.in0(IN), .in1(32'h10), .out(OUT), .sel(comparator_1_lt));
endmodule

module keyboard (
  input  INT_ACK,
  input  CLK,
  output [31:0] ADDR_BUS,
  output [31:0] DATA,
  output INT
);

  wire keyboard_1_avail, register_1_q, register_2_q;
  wire [6:0] keyboard_1_data;

  Register #(.width(1)) register_1 (.D(INT_ACK), .en(1'b1), .Q(register_1_q), .clk(CLK));  // open: clr
  Keyboard keyboard_1 (.clk(register_2_q), .avail(keyboard_1_avail), .data(keyboard_1_data));  // open: re, clr
  Register #(.width(1)) register_2 (.D(register_1_q), .en(1'b1), .Q(register_2_q), .clk(CLK));  // open: clr
  assign INT = keyboard_1_avail ? 1'b1 : 1'bz;  // Controlled_Buffer controlled_buffer_1
  assign ADDR_BUS = INT_ACK ? 32'h2 : 32'bz;  // Controlled_Buffer controlled_buffer_2
  assign DATA = INT_ACK ? {{25{1'b0}}, keyboard_1_data} : 32'bz;  // Controlled_Buffer controlled_buffer_3
endmodule
