// Logisim project lastname_firstname.circ as structural Verilog
module main (
  input  TEST_STALL
);

  wire BRANCH_TAKEN, BUFFERED_BRANCH_TAKEN, CLK, fwd_logic_1_stall, not_1_out, or_2_out, STALL, STALLED,
       WR_REG;
  wire [3:0] EX_OP, idrr_ex_buffer_1_dst_reg_2, idrr_ex_buffer_1_opcode_2, REG_1, REG_2,
       split_instruction_1_opcode, split_instruction_1_rx, WR_REG_NO;
  wire [19:0] split_instruction_1_off;
  wire [23:0] adder_1_out, ADDR, BEQ_LOC, idrr_ex_buffer_1_old_pc_2, if_idrr_buffer_1_pc_2, NEW_PC, PC;
  wire [31:0] DATA, execute_1_result, idrr_ex_buffer_1_offset_2, idrr_ex_buffer_1_val_1_2,
       idrr_ex_buffer_1_val_2_2, if_idrr_buffer_1_instruction_2, NEXT_INSTRUCTION, REG_1_CUR, REG_2_CUR,
       SAFE_R1, SAFE_R2, sext_20_1_out, WR_REG_DATA;

  Clock clock_1 (.out(CLK));
  Register #(.width(24)) u_PC (.D(NEW_PC), .en(not_1_out), .Q(PC), .clk(CLK));  // open: clr
  not not_1 (not_1_out, STALL);
  Adder #(.width(24)) adder_1 (.a(PC), .b(24'h1), .out(adder_1_out));  // open: cin, cout
  fwd_logic fwd_logic_1 (
    .READ_1(EX_OP), .READ_1_CUR(REG_1_CUR), .READ_2(REG_2), .READ_2_CUR(REG_2_CUR), .VAL_1(SAFE_R1),
    .VAL_2(SAFE_R2), .STALL(fwd_logic_1_stall), .EX_OPCODE(REG_1));  // open: EX_DST, EX_VAL, MEM_DST, MEM_VAL, WB_DST, WB_VAL
  Multiplexer #(.width(24), .enable("false")) multiplexer_1 (
    .in0(adder_1_out), .in1(BEQ_LOC), .out(NEW_PC), .sel(BRANCH_TAKEN));
  Dual_Ported_Register_File dual_ported_register_file_1 (
    .CLK(CLK), .WrREGNO(WR_REG_NO), .RdREGNO1(REG_1), .RdREGNO2(REG_2), .INPUT(WR_REG_DATA),
    .OUT1(REG_1_CUR), .OUT2(REG_2_CUR), .WrEN(WR_REG));
  or or_1 (STALL, TEST_STALL, fwd_logic_1_stall);
  IF_IDRR_Buffer if_idrr_buffer_1 (
    .PC(PC), .INSTRUCTION(NEXT_INSTRUCTION), .PC_2(if_idrr_buffer_1_pc_2),
    .INSTRUCTION_2(if_idrr_buffer_1_instruction_2), .CLK(CLK), .CLEAR(BUFFERED_BRANCH_TAKEN), .STALL(STALL));
  split_instruction split_instruction_1 (
    .INSTRUCTION(if_idrr_buffer_1_instruction_2), .OPCODE(split_instruction_1_opcode),
    .RX(split_instruction_1_rx), .RY(REG_1), .RZ(REG_2), .OFF(split_instruction_1_off));
  Register #(.width(1)) register_1 (.D(BRANCH_TAKEN), .Q(BUFFERED_BRANCH_TAKEN), .clk(CLK), .clr(1'b1));  // open: en
  Register #(.width(1)) register_2 (.D(STALL), .Q(STALLED), .clk(CLK), .clr(1'b1));  // open: en
  RAM #(.addrWidth(24), .dataWidth(32)) ram_1 (.addr(PC), .data(NEXT_INSTRUCTION), .clk(CLK));  // open: sel, ld, clr
  RAM #(.addrWidth(24), .dataWidth(32)) ram_2 (.addr(ADDR), .data(DATA), .clk(CLK));  // open: sel, ld, clr
  sext_20 sext_20_1 (.IN(split_instruction_1_off), .OUT(sext_20_1_out));
  IDRR_EX_Buffer idrr_ex_buffer_1 (
    .OLD_PC(if_idrr_buffer_1_pc_2), .DST_REG(split_instruction_1_rx), .VAL_1(REG_1_CUR), .VAL_2(REG_2_CUR),
    .OLD_PC_2(idrr_ex_buffer_1_old_pc_2), .DST_REG_2(idrr_ex_buffer_1_dst_reg_2),
    .VAL_1_2(idrr_ex_buffer_1_val_1_2), .VAL_2_2(idrr_ex_buffer_1_val_2_2), .CLK(CLK),
    .OPCODE(split_instruction_1_opcode), .OPCODE_2(idrr_ex_buffer_1_opcode_2), .OFFSET(sext_20_1_out),
    .OFFSET_2(idrr_ex_buffer_1_offset_2), .CLEAR(or_2_out));
  or or_2 (or_2_out, STALLED, BUFFERED_BRANCH_TAKEN);
  Execute execute_1 (
    .PC(idrr_ex_buffer_1_old_pc_2), .VAL_1(idrr_ex_buffer_1_val_1_2), .OPCODE(idrr_ex_buffer_1_opcode_2),
    .VAL_2(idrr_ex_buffer_1_val_2_2), .OFFSET(idrr_ex_buffer_1_offset_2), .RESULT(execute_1_result),
    .BR_LOC(BEQ_LOC), .BRANCH_TAKEN(BRANCH_TAKEN));

  // Notes on the sheet:
  //   FETCH
  //   IMEM
  //   MEM
  //   DECODE
  //   EXECUTE
endmodule

module Dual_Ported_Register_File (
  input  CLK,
  input  WrEN,
  input  [3:0] WrREGNO,
  input  [3:0] RdREGNO1,
  input  [3:0] RdREGNO2,
  input  [31:0] INPUT,
  output [31:0] OUT1,
  output [31:0] OUT2
);

  wire En_a0, En_a1, En_a2, En_a3, En_a4, En_at, En_fp, En_k0, En_ra, En_s0, En_s1, En_s2, En_s3, En_sp,
       En_v0;
  wire [31:0] a0, a1, a2, a3, a4, at, fp, k0, ra, s0, s1, s2, s3, sp, v0, zero;

  Decoder #(.select(4), .disabled(0)) decoder_1 (
    .out1(En_at), .out2(En_v0), .out3(En_a0), .out4(En_a1), .out5(En_a2), .out6(En_a3), .out7(En_a4),
    .out8(En_s0), .out9(En_s1), .out10(En_s2), .out11(En_s3), .out12(En_k0), .out13(En_sp), .out14(En_fp),
    .out15(En_ra), .sel(WrREGNO), .en(WrEN));  // open: out0
  Register #(.width(32)) u_zero (.D(INPUT), .en(1'b0), .Q(zero), .clk(CLK));  // open: clr
  Register #(.width(32)) u_at (.D(INPUT), .en(En_at), .Q(at), .clk(CLK));  // open: clr
  Register #(.width(32)) u_v0 (.D(INPUT), .en(En_v0), .Q(v0), .clk(CLK));  // open: clr
  Register #(.width(32)) u_a0 (.D(INPUT), .en(En_a0), .Q(a0), .clk(CLK));  // open: clr
  Register #(.width(32)) u_a1 (.D(INPUT), .en(En_a1), .Q(a1), .clk(CLK));  // open: clr
  Register #(.width(32)) u_a2 (.D(INPUT), .en(En_a2), .Q(a2), .clk(CLK));  // open: clr
  Register #(.width(32)) u_a3 (.D(INPUT), .en(En_a3), .Q(a3), .clk(CLK));  // open: clr
  Register #(.width(32)) u_a4 (.D(INPUT), .en(En_a4), .Q(a4), .clk(CLK));  // open: clr
  Multiplexer #(.select(4), .width(32), .disabled(0), .enable("false")) multiplexer_1 (
    .in0(zero), .in1(at), .in2(v0), .in3(a0), .in4(a1), .in5(a2), .in6(a3), .in7(a4), .in8(s0), .in9(s1),
    .in10(s2), .in11(s3), .in12(k0), .in13(sp), .in14(fp), .in15(ra), .out(OUT2), .sel(RdREGNO2));
  Register #(.width(32)) u_s0 (.D(INPUT), .en(En_s0), .Q(s0), .clk(CLK));  // open: clr
  Register #(.width(32)) u_s1 (.D(INPUT), .en(En_s1), .Q(s1), .clk(CLK));  // open: clr
  Register #(.width(32)) u_s2 (.D(INPUT), .en(En_s2), .Q(s2), .clk(CLK));  // open: clr
  Register #(.width(32)) u_s3 (.D(INPUT), .en(En_s3), .Q(s3), .clk(CLK));  // open: clr
  Register #(.width(32)) u_k0 (.D(INPUT), .en(En_k0), .Q(k0), .clk(CLK));  // open: clr
  Register #(.width(32)) u_sp (.D(INPUT), .en(En_sp), .Q(sp), .clk(CLK));  // open: clr
  Register #(.width(32)) u_fp (.D(INPUT), .en(En_fp), .Q(fp), .clk(CLK));  // open: clr
  Register #(.width(32)) u_ra (.D(INPUT), .en(En_ra), .Q(ra), .clk(CLK));  // open: clr
  Multiplexer #(.select(4), .width(32), .disabled(0), .enable("false")) multiplexer_2 (
    .in0(zero), .in1(at), .in2(v0), .in3(a0), .in4(a1), .in5(a2), .in6(a3), .in7(a4), .in8(s0), .in9(s1),
    .in10(s2), .in11(s3), .in12(k0), .in13(sp), .in14(fp), .in15(ra), .out(OUT1), .sel(RdREGNO1));

  // Notes on the sheet:
  //   MODIFY AT YOUR OWN RISK
endmodule

module IF_IDRR_Buffer (
  input  STALL,
  input  [23:0] PC,
  input  [31:0] INSTRUCTION,
  input  CLK,
  input  CLEAR,
  output [23:0] PC_2,
  output [31:0] INSTRUCTION_2
);

  wire not_1_out, not_2_out;

  not not_1 (not_1_out, STALL);
  Register #(.width(32)) register_1 (.D(INSTRUCTION), .en(not_2_out), .Q(INSTRUCTION_2), .clk(CLK), .clr(CLEAR));
  not not_2 (not_2_out, STALL);
  Register #(.width(24)) register_2 (.D(PC), .en(not_1_out), .Q(PC_2), .clk(CLK), .clr(CLEAR));
endmodule

module IDRR_EX_Buffer (
  input  [23:0] OLD_PC,
  input  CLK,
  input  CLEAR,
  input  [3:0] DST_REG,
  input  [31:0] VAL_1,
  input  [31:0] VAL_2,
  input  [31:0] OFFSET,
  input  [3:0] OPCODE,
  output [23:0] OLD_PC_2,
  output [3:0] DST_REG_2,
  output [31:0] VAL_1_2,
  output [31:0] VAL_2_2,
  output [31:0] OFFSET_2,
  output [3:0] OPCODE_2
);

  Register #(.width(24)) register_1 (.D(OLD_PC), .Q(OLD_PC_2), .clk(CLK), .clr(CLEAR));  // open: en
  Register #(.width(4)) register_2 (.D(DST_REG), .Q(DST_REG_2), .clk(CLK), .clr(CLEAR));  // open: en
  Register #(.width(32)) register_3 (.D(VAL_1), .Q(VAL_1_2), .clk(CLK), .clr(CLEAR));  // open: en
  Register #(.width(32)) register_4 (.D(VAL_2), .Q(VAL_2_2), .clk(CLK), .clr(CLEAR));  // open: en
  Register #(.width(32)) register_5 (.D(OFFSET), .Q(OFFSET_2), .clk(CLK), .clr(CLEAR));  // open: en
  Register #(.width(4)) register_6 (.D(OPCODE), .Q(OPCODE_2), .clk(CLK), .clr(CLEAR));  // open: en
endmodule

module ALU (
  input  [1:0] FUNC,
  input  [31:0] A,
  input  [31:0] B,
  output [31:0] OUT
);

  wire [31:0] adder_1_out, adder_2_out, nand_1_out, subtractor_1_out;

  Adder #(.width(32)) adder_1 (.a(A), .b(B), .out(adder_1_out), .cin(1'b0));  // open: cout
  assign nand_1_out = ~(A & B);  // NAND_Gate nand_1, 32 bits wide
  Subtractor #(.width(32)) subtractor_1 (.a(A), .b(B), .out(subtractor_1_out), .bin(1'b0));  // open: bout
  Adder #(.width(32)) adder_2 (.a(A), .b({32{1'b0}}), .out(adder_2_out), .cin(1'b1));  // open: cout
  Multiplexer #(.select(2), .width(32), .disabled(0), .enable("false")) multiplexer_1 (
    .in0(adder_1_out), .in1(nand_1_out), .in2(subtractor_1_out), .in3(adder_2_out), .out(OUT), .sel(FUNC));

  // Notes on the sheet:
  //   MODIFY AT YOUR OWN RISK
endmodule

module fwd_logic (
  input  [3:0] EX_OPCODE,
  input  [3:0] READ_1,
  input  [31:0] READ_1_CUR,
  input  [3:0] READ_2,
  input  [31:0] READ_2_CUR,
  input  [3:0] EX_DST,
  input  [31:0] EX_VAL,
  input  [3:0] MEM_DST,
  input  [31:0] MEM_VAL,
  input  [3:0] WB_DST,
  input  [31:0] WB_VAL,
  output [31:0] VAL_1,
  output [31:0] VAL_2,
  output STALL
);

  wire and_1_out, and_2_out, and_3_out, comparator_1_eq, comparator_2_eq, comparator_3_eq, comparator_4_eq,
       comparator_5_eq, comparator_6_eq, comparator_7_eq, comparator_8_eq, comparator_9_eq, comparator_10_eq,
       comparator_11_gt, comparator_11_lt, not_1_out, or_1_out, or_2_out;
  wire [1:0] _1SEL, _2SEL, opcode_to_type_1_out_2;

  not not_1 (not_1_out, and_1_out);
  // AND_Gate and_1 has open pins: out=and_1_out
  opcode_to_type opcode_to_type_1 (.OPCODE(EX_OPCODE), .out_2(opcode_to_type_1_out_2));
  Comparator #(.width(4)) comparator_1 (.a(READ_1), .b(WB_DST), .eq(comparator_1_eq));  // open: gt, lt
  Comparator #(.width(4)) comparator_2 (.a(READ_1), .b(MEM_DST), .eq(comparator_2_eq));  // open: gt, lt
  Comparator #(.width(4)) comparator_3 (.a(READ_1), .b(EX_DST), .eq(comparator_3_eq));  // open: gt, lt
  Comparator #(.width(4)) comparator_4 (.a(READ_1), .b(4'b0000), .eq(comparator_4_eq));  // open: gt, lt
  Comparator #(.width(4)) comparator_5 (.a(READ_2), .b(WB_DST), .eq(comparator_5_eq));  // open: gt, lt
  Comparator #(.width(4)) comparator_6 (.a(READ_2), .b(MEM_DST), .eq(comparator_6_eq));  // open: gt, lt
  Comparator #(.width(4)) comparator_7 (.a(READ_2), .b(EX_DST), .eq(comparator_7_eq));  // open: gt, lt
  Comparator #(.width(4)) comparator_8 (.a(READ_2), .b(4'b0000), .eq(comparator_8_eq));  // open: gt, lt
  Comparator #(.width(2)) comparator_9 (.a(_2SEL), .b(2'b10), .eq(comparator_9_eq));  // open: gt, lt
  Comparator #(.width(2)) comparator_10 (.a(_1SEL), .b(2'b10), .eq(comparator_10_eq));  // open: gt, lt
  and and_2 (and_2_out, comparator_3_eq, not_1_out);
  or or_1 (or_1_out, comparator_8_eq, comparator_11_gt, comparator_11_lt);
  Comparator #(.width(2)) comparator_11 (
    .a(opcode_to_type_1_out_2), .b(2'b00), .gt(comparator_11_gt), .lt(comparator_11_lt));  // open: eq
  and and_3 (and_3_out, EX_OPCODE[0], EX_OPCODE[1], ~EX_OPCODE[2], ~EX_OPCODE[3]);  // AND_Gate
  or or_2 (or_2_out, comparator_9_eq, comparator_10_eq);
  Priority_Encoder #(.select(2)) priority_encoder_1 (
    .in0(comparator_1_eq), .in1(comparator_2_eq), .in2(and_2_out), .in3(comparator_4_eq), .out(_1SEL),
    .en_in(1'b1));  // open: gs, en_out
  Priority_Encoder #(.select(2)) priority_encoder_2 (
    .in0(comparator_5_eq), .in1(comparator_6_eq), .in2(comparator_7_eq), .in3(or_1_out), .out(_2SEL),
    .en_in(1'b1));  // open: gs, en_out
  and and_4 (STALL, and_3_out, or_2_out);
  Multiplexer #(.select(2), .width(32), .enable("false")) multiplexer_1 (
    .in0(WB_VAL), .in1(MEM_VAL), .in2(EX_VAL), .in3(READ_1_CUR), .out(VAL_1), .sel(_1SEL));
  Multiplexer #(.select(2), .width(32), .enable("false")) multiplexer_2 (
    .in0(WB_VAL), .in1(MEM_VAL), .in2(EX_VAL), .in3(READ_2_CUR), .out(VAL_2), .sel(_2SEL));

  // Other names for the same wires on the sheet: EX[3:0] = EX_DST; MEM[3:0] = MEM_DST; OPCODE[3:0] = EX_OPCODE;
  //   R1[3:0] = READ_1; R1_VAL[31:0] = READ_1_CUR; R2[3:0] = READ_2; R2_VAL[31:0] = READ_2_CUR; WB[3:0] = WB_DST

  // Notes on the sheet:
  //   ONLY FORWARD RZ for R Types
  //   Check if EX has a load
  //   And we are forwarding from EX
endmodule

module split_instruction (
  input  [31:0] INSTRUCTION,
  output [3:0] OPCODE,
  output [3:0] RX,
  output [3:0] RY,
  output [3:0] RZ,
  output [19:0] OFF
);


  assign OFF = INSTRUCTION[19:0];
  assign OPCODE = INSTRUCTION[31:28];
  assign RX = INSTRUCTION[27:24];
  assign RY = INSTRUCTION[23:20];
  assign RZ = INSTRUCTION[3:0];
endmodule

module opcode_to_type (
  input  [3:0] OPCODE,
  output [1:0] out_2
);

  wire and_1_out, and_2_out, and_3_out;

  and and_1 (and_1_out, ~OPCODE[1], ~OPCODE[2], ~OPCODE[3]);  // AND_Gate
  and and_2 (and_2_out, ~OPCODE[3], OPCODE[2], OPCODE[1], ~OPCODE[0]);  // AND_Gate
  and and_3 (and_3_out, ~and_1_out, ~and_2_out);  // AND_Gate
  Priority_Encoder #(.select(2)) priority_encoder_1 (
    .in0(and_1_out), .in1(and_3_out), .in2(and_2_out), .out(out_2), .en_in(1'b1));  // open: in3, gs, en_out

  // Notes on the sheet:
  //   0: R-Type
  //   1: I-Type
  //   2: J-Type
endmodule

module sext_20 (
  input  [19:0] IN,
  output [31:0] OUT
);


  assign OUT = {{13{IN[19]}}, IN[18:0]};
endmodule

module Execute (
  input  [31:0] VAL_1,
  input  [3:0] OPCODE,
  input  [31:0] VAL_2,
  input  [23:0] PC,
  input  [31:0] OFFSET,
  output [31:0] RESULT,
  output BRANCH_TAKEN,
  output [23:0] BR_LOC
);

  wire chkZ, comparator_1_gt, comparator_1_lt, comparator_2_eq, or_1_out;
  wire [1:0] FUNC, opcode_to_type_1_out_2;
  wire [31:0] multiplexer_1_out;
  wire [31:3] rom_1_data;

  ROM #(.addrWidth(4), .dataWidth(32)) rom_1 (.addr(OPCODE), .data({rom_1_data, chkZ, FUNC}));  // open: sel
  Adder #(.width(24)) adder_1 (.a(PC), .b(OFFSET[23:0]), .out(BR_LOC));  // open: cin, cout
  opcode_to_type opcode_to_type_1 (.OPCODE(OPCODE), .out_2(opcode_to_type_1_out_2));
  Multiplexer #(.width(32), .enable("false")) multiplexer_1 (
    .in0(VAL_2), .in1(OFFSET), .out(multiplexer_1_out), .sel(or_1_out));
  Comparator #(.width(2)) comparator_1 (
    .a(opcode_to_type_1_out_2), .b(2'b00), .gt(comparator_1_gt), .lt(comparator_1_lt));  // open: eq
  or or_1 (or_1_out, comparator_1_gt, comparator_1_lt);
  ALU alu_1 (.FUNC(FUNC), .A(VAL_1), .B(multiplexer_1_out), .OUT(RESULT));
  Comparator #(.width(32)) comparator_2 (.a(RESULT), .b({32{1'b0}}), .eq(comparator_2_eq));  // open: gt, lt
  and and_1 (BRANCH_TAKEN, comparator_2_eq, chkZ);
endmodule
