// Logisim project peteet_henry.circ as structural Verilog: 10 circuits, main circuit main
module main (
  output [31:0] out_1
);

  wire and_1_out, BRANCH_TAKEN, CHK_Z, CLK, cnt_sig_convert_1_off_to_alu, comparator_1_eq, EX_JMP,
       EX_WRITE_REG, FWD_STALL, HALT, LD_IN_EX, MEM_WR_REG, not_1_out, not_2_out, or_1_out, READ_MEM, STALL,
       WR_REG_WB, WRITE_MEM;
  wire [1:0] cnt_sig_convert_1_alu_func;
  wire [3:0] decode_logic_1_dst, decode_logic_1_opcode, EX_DST, MEM_DST, RREG1_NO, RREG2_NO, WR_REG_NO;
  wire [31:0] adder_2_out, BRANCH_LOC, decode_logic_1_control_signals, decode_logic_1_offset, DMEM_DATA,
       ex_mem_buffer_1_cnt_sig_2, EX_PC, EX_RES, FWD_VAL_1, FWD_VAL_2, idrr_ex_buffer_1_cnt_sig_2,
       if_idrr_buffer_1_instruction_2, if_idrr_buffer_1_pc_2, IMEM_DATA, MEM_RES, mem_wb_buffer_1_cnt_sig_2,
       multiplexer_1_out, multiplexer_2_out, multiplexer_3_out, OFFSET_EX, PC_1, RESULT, VAL_1, VAL_1_EX,
       VAL_2, VAL_2_EX, VAL_2_MEM, WR_REG_VAL;

  Clock clock_1 (.out(CLK));
  Multiplexer #(.width(32), .enable("false")) multiplexer_1 (
    .in0(PC_1), .in1(BRANCH_LOC), .out(multiplexer_1_out), .sel(BRANCH_TAKEN));
  or or_1 (or_1_out, ~STALL, BRANCH_TAKEN);  // OR_Gate
  // Probe on PC_1
  Register #(.width(32)) PC (.D(multiplexer_1_out), .en(or_1_out), .Q(out_1), .clk(CLK));  // open: clr
  IF_IDRR_Buffer if_idrr_buffer_1 (
    .PC(PC_1), .INSTRUCTION(IMEM_DATA), .PC_2(if_idrr_buffer_1_pc_2),
    .INSTRUCTION_2(if_idrr_buffer_1_instruction_2), .CLK(CLK), .WE(not_1_out), .CLEAR(BRANCH_TAKEN));
  not not_1 (not_1_out, STALL);
  Adder #(.width(32)) adder_1 (.a(out_1), .b(32'h1), .out(PC_1));  // open: cin, cout
  FWD_MAGICS fwd_magics_1 (
    .SR_1(RREG1_NO), .VAL_1(VAL_1), .SR_2(RREG2_NO), .VAL_2(VAL_2), .EX_CHANGES_REG(EX_WRITE_REG),
    .EX_DST_REG(EX_DST), .EX_RES(EX_RES), .MEM_CHANGES_REG(MEM_WR_REG), .MEM_DST_REG(MEM_DST),
    .MEM_RES(MEM_RES), .WB_CHANGES_REG(WR_REG_WB), .WB_DST_REG(WR_REG_NO), .WB_RES(WR_REG_VAL),
    .VAL_1_2(FWD_VAL_1), .VAL_2_2(FWD_VAL_2), .LD_IN_EX(LD_IN_EX), .SHOULD_STALL(FWD_STALL));
  // Probe on if_idrr_buffer_1_pc_2
  DECODE_LOGIC decode_logic_1 (
    .INSTRUCTION(if_idrr_buffer_1_instruction_2), .OPCODE(decode_logic_1_opcode), .SR_1(RREG1_NO),
    .SR_2(RREG2_NO), .OFFSET(decode_logic_1_offset), .CONTROL_SIGNALS(decode_logic_1_control_signals),
    .DST(decode_logic_1_dst));
  // Probe on RREG1_NO
  // Probe on RREG2_NO
  // Probe on decode_logic_1_offset
  // Probe on decode_logic_1_dst
  // Probe on FWD_VAL_1
  IDRR_EX_Buffer idrr_ex_buffer_1 (
    .OPCODE(decode_logic_1_opcode), .CNT_SIG(decode_logic_1_control_signals), .VAL_1(FWD_VAL_1),
    .VAL_2(FWD_VAL_2), .OFFSET(decode_logic_1_offset), .PC(if_idrr_buffer_1_pc_2), .CLK(CLK), .PC_2(EX_PC),
    .CNT_SIG_2(idrr_ex_buffer_1_cnt_sig_2), .VAL_1_2(VAL_1_EX), .VAL_2_2(VAL_2_EX), .OFFSET_2(OFFSET_EX),
    .DST(decode_logic_1_dst), .DST_2(EX_DST), .BUBBLE(STALL));  // open: OPCODE_2
  // Probe on FWD_VAL_2
  // Probe on EX_PC
  Dual_Ported_Register_File dual_ported_register_file_1 (
    .CLK(CLK), .WrREGNO(WR_REG_NO), .RdREGNO1(RREG1_NO), .RdREGNO2(RREG2_NO), .INPUT(WR_REG_VAL),
    .OUT1(VAL_1), .OUT2(VAL_2), .WrEN(WR_REG_WB));
  CNT_SIG_CONVERT cnt_sig_convert_1 (
    .CNT_SIG(idrr_ex_buffer_1_cnt_sig_2), .WR_REG(EX_WRITE_REG), .ALU_FUNC(cnt_sig_convert_1_alu_func),
    .OFF_TO_ALU(cnt_sig_convert_1_off_to_alu), .CHK_Z(CHK_Z), .STALL(LD_IN_EX), .HALT(HALT), .JMP(EX_JMP));  // open: RX, RY, RZ, SR_1, SR_2, DST, WR_MEM, READ_MEM
  // Probe on RESULT[23:0]
  or or_2 (STALL, BRANCH_TAKEN, FWD_STALL);
  // Probe on cnt_sig_convert_1_alu_func
  RAM #(.addrWidth(24), .dataWidth(32)) ram_1 (.addr(out_1[23:0]), .data(IMEM_DATA), .clk(CLK));  // open: sel, ld, clr
  RAM #(.addrWidth(24), .dataWidth(32)) ram_2 (
    .addr(RESULT[23:0]), .data(DMEM_DATA), .clk(CLK), .ld(not_2_out));  // open: sel, clr
  not not_2 (not_2_out, WRITE_MEM);
  Multiplexer #(.width(32), .enable("false")) multiplexer_2 (
    .in0(VAL_1_EX), .in1(EX_PC), .out(multiplexer_2_out), .sel(EX_JMP));
  // Probe on multiplexer_3_out
  Multiplexer #(.width(32), .enable("false")) multiplexer_3 (
    .in0(VAL_2_EX), .in1(OFFSET_EX), .out(multiplexer_3_out), .sel(cnt_sig_convert_1_off_to_alu));
  assign DMEM_DATA = WRITE_MEM ? VAL_2_MEM : 32'bz;  // Controlled_Buffer controlled_buffer_1
  // Probe on DMEM_DATA
  // Probe on multiplexer_2_out
  Adder #(.width(32)) adder_2 (.a(OFFSET_EX), .b(EX_PC), .out(adder_2_out));  // open: cin, cout
  ALU alu_1 (.FUNC(cnt_sig_convert_1_alu_func), .A(multiplexer_2_out), .B(multiplexer_3_out), .OUT(EX_RES));
  Multiplexer #(.width(32), .enable("false")) multiplexer_4 (
    .in0(adder_2_out), .in1(VAL_1_EX), .out(BRANCH_LOC), .sel(EX_JMP));
  // Probe on EX_RES
  Comparator #(.width(32)) comparator_1 (.a(EX_RES), .b({32{1'b0}}), .eq(comparator_1_eq));  // open: gt, lt
  and and_1 (and_1_out, CHK_Z, comparator_1_eq);
  or or_3 (BRANCH_TAKEN, EX_JMP, and_1_out);
  EX_MEM_Buffer ex_mem_buffer_1 (
    .CNT_SIG(idrr_ex_buffer_1_cnt_sig_2), .RES(EX_RES), .OFFSET(OFFSET_EX),
    .CNT_SIG_2(ex_mem_buffer_1_cnt_sig_2), .RES_2(RESULT), .CLK(CLK), .VAL_1(VAL_2_EX), .VAL_1_2(VAL_2_MEM),
    .DST(EX_DST), .DST_2(MEM_DST));  // open: OFFSET_2
  // Probe on EX_DST
  CNT_SIG_CONVERT cnt_sig_convert_2 (
    .CNT_SIG(ex_mem_buffer_1_cnt_sig_2), .WR_REG(MEM_WR_REG), .WR_MEM(WRITE_MEM), .READ_MEM(READ_MEM));  // open: RX, RY, RZ, ALU_FUNC, SR_1, SR_2, DST, OFF_TO_ALU, CHK_Z, STALL, HALT, JMP
  // Probe on MEM_RES
  Multiplexer #(.width(32), .enable("false")) multiplexer_5 (
    .in0(RESULT), .in1(DMEM_DATA), .out(MEM_RES), .sel(READ_MEM));
  MEM_WB_Buffer mem_wb_buffer_1 (
    .CNT_SIG(ex_mem_buffer_1_cnt_sig_2), .RES(MEM_RES), .CNT_SIG_2(mem_wb_buffer_1_cnt_sig_2),
    .RES_2(WR_REG_VAL), .CLK(CLK), .DST(MEM_DST), .DST_2(WR_REG_NO));
  // Probe on WR_REG_NO
  // Probe on WR_REG_VAL
  CNT_SIG_CONVERT cnt_sig_convert_3 (
    .CNT_SIG(mem_wb_buffer_1_cnt_sig_2), .WR_REG(WR_REG_WB));  // open: RX, RY, RZ, ALU_FUNC, SR_1, SR_2, DST, OFF_TO_ALU, WR_MEM, READ_MEM, CHK_Z, STALL, HALT, JMP

  // Other names for the same wires on the sheet: IMEM_ADDR[31:0] = out_1; PC[31:0] = out_1

  // Notes on the sheet:
  //   FETCH
  //   DECODE
  //   EXECUTE
  //   MEM
  //   WRITE BACK
endmodule

module Dual_Ported_Register_File (
  input  CLK,
  input  WrEN,
  input  [3:0] WrREGNO,
  input  [3:0] RdREGNO1,
  input  [3:0] RdREGNO2,
  input  [31:0] INPUT,
  output [31:0] OUT1,
  output [31:0] OUT2
);

  wire En_a0, En_a1, En_a2, En_a3, En_a4, En_at, En_fp, En_k0, En_ra, En_s0, En_s1, En_s2, En_s3, En_sp,
       En_v0;
  wire [31:0] a0, a1, a2, a3, a4, at, fp, k0, ra, s0, s1, s2, s3, sp, v0, zero;

  Decoder #(.select(4), .disabled(0)) decoder_1 (
    .out1(En_at), .out2(En_v0), .out3(En_a0), .out4(En_a1), .out5(En_a2), .out6(En_a3), .out7(En_a4),
    .out8(En_s0), .out9(En_s1), .out10(En_s2), .out11(En_s3), .out12(En_k0), .out13(En_sp), .out14(En_fp),
    .out15(En_ra), .sel(WrREGNO), .en(WrEN));  // open: out0
  Register #(.width(32)) u_zero (.D(INPUT), .en(1'b0), .Q(zero), .clk(CLK));  // open: clr
  Register #(.width(32)) u_at (.D(INPUT), .en(En_at), .Q(at), .clk(CLK));  // open: clr
  Register #(.width(32)) u_v0 (.D(INPUT), .en(En_v0), .Q(v0), .clk(CLK));  // open: clr
  Register #(.width(32)) u_a0 (.D(INPUT), .en(En_a0), .Q(a0), .clk(CLK));  // open: clr
  Register #(.width(32)) u_a1 (.D(INPUT), .en(En_a1), .Q(a1), .clk(CLK));  // open: clr
  Register #(.width(32)) u_a2 (.D(INPUT), .en(En_a2), .Q(a2), .clk(CLK));  // open: clr
  Register #(.width(32)) u_a3 (.D(INPUT), .en(En_a3), .Q(a3), .clk(CLK));  // open: clr
  Register #(.width(32)) u_a4 (.D(INPUT), .en(En_a4), .Q(a4), .clk(CLK));  // open: clr
  Multiplexer #(.select(4), .width(32), .disabled(0), .enable("false")) multiplexer_1 (
    .in0(zero), .in1(at), .in2(v0), .in3(a0), .in4(a1), .in5(a2), .in6(a3), .in7(a4), .in8(s0), .in9(s1),
    .in10(s2), .in11(s3), .in12(k0), .in13(sp), .in14(fp), .in15(ra), .out(OUT2), .sel(RdREGNO2));
  Register #(.width(32)) u_s0 (.D(INPUT), .en(En_s0), .Q(s0), .clk(CLK));  // open: clr
  Register #(.width(32)) u_s1 (.D(INPUT), .en(En_s1), .Q(s1), .clk(CLK));  // open: clr
  Register #(.width(32)) u_s2 (.D(INPUT), .en(En_s2), .Q(s2), .clk(CLK));  // open: clr
  Register #(.width(32)) u_s3 (.D(INPUT), .en(En_s3), .Q(s3), .clk(CLK));  // open: clr
  Register #(.width(32)) u_k0 (.D(INPUT), .en(En_k0), .Q(k0), .clk(CLK));  // open: clr
  Register #(.width(32)) u_sp (.D(INPUT), .en(En_sp), .Q(sp), .clk(CLK));  // open: clr
  Register #(.width(32)) u_fp (.D(INPUT), .en(En_fp), .Q(fp), .clk(CLK));  // open: clr
  Register #(.width(32)) u_ra (.D(INPUT), .en(En_ra), .Q(ra), .clk(CLK));  // open: clr
  Multiplexer #(.select(4), .width(32), .disabled(0), .enable("false")) multiplexer_2 (
    .in0(zero), .in1(at), .in2(v0), .in3(a0), .in4(a1), .in5(a2), .in6(a3), .in7(a4), .in8(s0), .in9(s1),
    .in10(s2), .in11(s3), .in12(k0), .in13(sp), .in14(fp), .in15(ra), .out(OUT1), .sel(RdREGNO1));

  // Notes on the sheet:
  //   MODIFY AT YOUR OWN RISK
endmodule

module IF_IDRR_Buffer (
  input  [31:0] PC,
  input  [31:0] INSTRUCTION,
  input  CLK,
  input  WE,
  input  CLEAR,
  output [31:0] PC_2,
  output [31:0] INSTRUCTION_2
);

  wire CLEAR_t;
  wire [31:0] register_1_q, register_2_q;

  Register #(.width(32)) register_1 (.D(PC), .en(WE), .Q(register_1_q), .clk(CLK));  // open: clr
  Register #(.width(32)) register_2 (.D(INSTRUCTION), .en(WE), .Q(register_2_q), .clk(CLK));  // open: clr
  Multiplexer #(.width(32)) multiplexer_1 (
    .in0(register_1_q), .in1({32{1'b0}}), .out(PC_2), .sel(CLEAR_t));  // open: en
  Multiplexer #(.width(32)) multiplexer_2 (
    .in0(register_2_q), .in1({32{1'b0}}), .out(INSTRUCTION_2), .sel(CLEAR_t));  // open: en
  Register #(.width(1)) register_3 (.D(CLEAR), .en(1'b1), .Q(CLEAR_t), .clk(CLK));  // open: clr
endmodule

module IDRR_EX_Buffer (
  input  [31:0] PC,
  input  [3:0] OPCODE,
  input  [31:0] CNT_SIG,
  input  [31:0] VAL_1,
  input  [31:0] VAL_2,
  input  [31:0] OFFSET,
  input  [3:0] DST,
  input  CLK,
  input  BUBBLE,
  output [31:0] PC_2,
  output [3:0] OPCODE_2,
  output [31:0] CNT_SIG_2,
  output [31:0] VAL_1_2,
  output [31:0] VAL_2_2,
  output [31:0] OFFSET_2,
  output [3:0] DST_2
);

  wire [3:0] multiplexer_4_out, multiplexer_6_out;
  wire [31:0] multiplexer_1_out, multiplexer_2_out, multiplexer_3_out, multiplexer_5_out, multiplexer_7_out;

  Multiplexer #(.width(32), .enable("false")) multiplexer_1 (
    .in0(VAL_1), .in1({32{1'b0}}), .out(multiplexer_1_out), .sel(BUBBLE));
  Multiplexer #(.width(32), .enable("false")) multiplexer_2 (
    .in0(VAL_2), .in1({32{1'b0}}), .out(multiplexer_2_out), .sel(BUBBLE));
  Multiplexer #(.width(32), .enable("false")) multiplexer_3 (
    .in0(OFFSET), .in1({32{1'b0}}), .out(multiplexer_3_out), .sel(BUBBLE));
  Multiplexer #(.width(4), .enable("false")) multiplexer_4 (
    .in0(DST), .in1(4'b0000), .out(multiplexer_4_out), .sel(BUBBLE));
  Multiplexer #(.width(32), .enable("false")) multiplexer_5 (
    .in0(PC), .in1({32{1'b0}}), .out(multiplexer_5_out), .sel(BUBBLE));
  Register #(.width(32)) register_1 (.D(multiplexer_5_out), .en(1'b1), .Q(PC_2), .clk(CLK));  // open: clr
  Register #(.width(4)) register_2 (.D(multiplexer_6_out), .en(1'b1), .Q(OPCODE_2), .clk(CLK));  // open: clr
  Multiplexer #(.width(4), .enable("false")) multiplexer_6 (
    .in0(OPCODE), .in1(4'b0000), .out(multiplexer_6_out), .sel(BUBBLE));
  Register #(.width(32)) register_3 (.D(multiplexer_7_out), .en(1'b1), .Q(CNT_SIG_2), .clk(CLK));  // open: clr
  Multiplexer #(.width(32), .enable("false")) multiplexer_7 (
    .in0(CNT_SIG), .in1({32{1'b0}}), .out(multiplexer_7_out), .sel(BUBBLE));
  Register #(.width(32)) register_4 (.D(multiplexer_1_out), .en(1'b1), .Q(VAL_1_2), .clk(CLK));  // open: clr
  Register #(.width(32)) register_5 (.D(multiplexer_2_out), .en(1'b1), .Q(VAL_2_2), .clk(CLK));  // open: clr
  Register #(.width(32)) register_6 (.D(multiplexer_3_out), .en(1'b1), .Q(OFFSET_2), .clk(CLK));  // open: clr
  Register #(.width(4)) register_7 (.D(multiplexer_4_out), .en(1'b1), .Q(DST_2), .clk(CLK));  // open: clr
endmodule

module EX_MEM_Buffer (
  input  [31:0] CNT_SIG,
  input  [31:0] RES,
  input  [31:0] VAL_1,
  input  [31:0] OFFSET,
  input  [3:0] DST,
  input  CLK,
  output [31:0] CNT_SIG_2,
  output [31:0] RES_2,
  output [31:0] VAL_1_2,
  output [31:0] OFFSET_2,
  output [3:0] DST_2
);

  Register #(.width(32)) register_1 (.D(CNT_SIG), .en(1'b1), .Q(CNT_SIG_2), .clk(CLK));  // open: clr
  Register #(.width(32)) register_2 (.D(RES), .en(1'b1), .Q(RES_2), .clk(CLK));  // open: clr
  Register #(.width(32)) register_3 (.D(VAL_1), .en(1'b1), .Q(VAL_1_2), .clk(CLK));  // open: clr
  Register #(.width(32)) register_4 (.D(OFFSET), .en(1'b1), .Q(OFFSET_2), .clk(CLK));  // open: clr
  Register #(.width(4)) register_5 (.D(DST), .en(1'b1), .Q(DST_2), .clk(CLK));  // open: clr
endmodule

module MEM_WB_Buffer (
  input  [31:0] CNT_SIG,
  input  [31:0] RES,
  input  [3:0] DST,
  input  CLK,
  output [31:0] CNT_SIG_2,
  output [31:0] RES_2,
  output [3:0] DST_2
);

  Register #(.width(32)) register_1 (.D(CNT_SIG), .en(1'b1), .Q(CNT_SIG_2), .clk(CLK));  // open: clr
  Register #(.width(32)) register_2 (.D(RES), .en(1'b1), .Q(RES_2), .clk(CLK));  // open: clr
  Register #(.width(4)) register_3 (.D(DST), .en(1'b1), .Q(DST_2), .clk(CLK));  // open: clr
endmodule

module ALU (
  input  [1:0] FUNC,
  input  [31:0] A,
  input  [31:0] B,
  output [31:0] OUT
);

  wire [31:0] adder_1_out, adder_2_out, nand_1_out, subtractor_1_out;

  Adder #(.width(32)) adder_1 (.a(A), .b(B), .out(adder_1_out), .cin(1'b0));  // open: cout
  assign nand_1_out = ~(A & B);  // NAND_Gate nand_1, 32 bits wide
  Subtractor #(.width(32)) subtractor_1 (.a(A), .b(B), .out(subtractor_1_out), .bin(1'b0));  // open: bout
  Adder #(.width(32)) adder_2 (.a(A), .b({32{1'b0}}), .out(adder_2_out), .cin(1'b1));  // open: cout
  Multiplexer #(.select(2), .width(32), .disabled(0), .enable("false")) multiplexer_1 (
    .in0(adder_1_out), .in1(nand_1_out), .in2(subtractor_1_out), .in3(adder_2_out), .out(OUT), .sel(FUNC));

  // Notes on the sheet:
  //   MODIFY AT YOUR OWN RISK
endmodule

module DECODE_LOGIC (
  input  [31:0] INSTRUCTION,
  output [3:0] OPCODE,
  output [3:0] DST,
  output [3:0] SR_1,
  output [3:0] SR_2,
  output [31:0] OFFSET,
  output [31:0] CONTROL_SIGNALS
);

  ROM #(.addrWidth(4), .dataWidth(32)) rom_1 (.addr(INSTRUCTION[31:28]), .data(CONTROL_SIGNALS));  // open: sel
  CNT_SIG_CONVERT cnt_sig_convert_1 (
    .CNT_SIG(CONTROL_SIGNALS), .RX(INSTRUCTION[27:24]), .RY(INSTRUCTION[23:20]), .RZ(INSTRUCTION[3:0]),
    .SR_1(SR_1), .SR_2(SR_2), .DST(DST));  // open: WR_REG, ALU_FUNC, OFF_TO_ALU, WR_MEM, READ_MEM, CHK_Z, STALL, HALT, JMP

  assign OFFSET = {{13{INSTRUCTION[19]}}, INSTRUCTION[18:0]};
  assign OPCODE = INSTRUCTION[31:28];

  // Other names for the same wires on the sheet: CNT_SIG[31:0] = CONTROL_SIGNALS; OFFSET_t[19:0] = INSTRUCTION[19:0];
  //   RZ[3:0] = INSTRUCTION[3:0]; RX[3:0] = INSTRUCTION[27:24]; RY[3:0] = INSTRUCTION[23:20]

  // Notes on the sheet:
  //   contents of rom_1 (hex, n*v repeats v):
  //   e2800000 e6800000 22c00000 22d40000 60600000 98080000 13090000
endmodule

module FWD_MAGICS (
  input  [3:0] SR_1,
  input  [31:0] VAL_1,
  input  [3:0] SR_2,
  input  [31:0] VAL_2,
  input  EX_CHANGES_REG,
  input  [3:0] EX_DST_REG,
  input  [31:0] EX_RES,
  input  MEM_CHANGES_REG,
  input  [3:0] MEM_DST_REG,
  input  [31:0] MEM_RES,
  input  WB_CHANGES_REG,
  input  [3:0] WB_DST_REG,
  input  [31:0] WB_RES,
  input  LD_IN_EX,
  output [31:0] VAL_1_2,
  output SHOULD_STALL,
  output [31:0] VAL_2_2
);

  wire and_1_out, and_2_out, and_3_out, and_4_out, and_5_out, and_6_out, and_7_out, and_8_out, and_9_out,
       and_10_out, and_11_out, and_12_out, and_13_out, and_14_out, comparator_1_eq, comparator_2_eq,
       comparator_3_eq, comparator_4_eq, comparator_5_eq, comparator_6_eq, comparator_7_eq, comparator_8_eq,
       comparator_9_eq, comparator_10_eq, comparator_11_eq, comparator_12_eq, comparator_13_eq,
       comparator_14_eq, or_1_out, or_2_out, or_3_out;
  wire [1:0] priority_encoder_1_out, priority_encoder_2_out;

  Comparator #(.width(4)) comparator_1 (.a(SR_1), .b(WB_DST_REG), .eq(comparator_1_eq));  // open: gt, lt
  Comparator #(.width(4)) comparator_2 (.a(WB_DST_REG), .b(4'b0000), .eq(comparator_2_eq));  // open: gt, lt
  Comparator #(.width(4)) comparator_3 (.a(SR_1), .b(MEM_DST_REG), .eq(comparator_3_eq));  // open: gt, lt
  Comparator #(.width(4)) comparator_4 (.a(MEM_DST_REG), .b(4'b0000), .eq(comparator_4_eq));  // open: gt, lt
  Comparator #(.width(4)) comparator_5 (.a(SR_1), .b(EX_DST_REG), .eq(comparator_5_eq));  // open: gt, lt
  Comparator #(.width(4)) comparator_6 (.a(EX_DST_REG), .b(4'b0000), .eq(comparator_6_eq));  // open: gt, lt
  Comparator #(.width(4)) comparator_7 (.a(SR_2), .b(WB_DST_REG), .eq(comparator_7_eq));  // open: gt, lt
  Comparator #(.width(4)) comparator_8 (.a(WB_DST_REG), .b(4'b0000), .eq(comparator_8_eq));  // open: gt, lt
  and and_1 (and_1_out, ~comparator_8_eq, WB_CHANGES_REG);  // AND_Gate
  Comparator #(.width(4)) comparator_9 (.a(SR_2), .b(MEM_DST_REG), .eq(comparator_9_eq));  // open: gt, lt
  Comparator #(.width(4)) comparator_10 (.a(MEM_DST_REG), .b(4'b0000), .eq(comparator_10_eq));  // open: gt, lt
  and and_2 (and_2_out, ~comparator_10_eq, MEM_CHANGES_REG);  // AND_Gate
  Comparator #(.width(4)) comparator_11 (.a(SR_2), .b(EX_DST_REG), .eq(comparator_11_eq));  // open: gt, lt
  Comparator #(.width(4)) comparator_12 (.a(EX_DST_REG), .b(4'b0000), .eq(comparator_12_eq));  // open: gt, lt
  and and_3 (and_3_out, ~comparator_12_eq, EX_CHANGES_REG);  // AND_Gate
  and and_4 (and_4_out, ~comparator_2_eq, WB_CHANGES_REG);  // AND_Gate
  and and_5 (and_5_out, ~comparator_4_eq, MEM_CHANGES_REG);  // AND_Gate
  and and_6 (and_6_out, ~comparator_6_eq, EX_CHANGES_REG);  // AND_Gate
  Comparator #(.width(4)) comparator_13 (.a(SR_1), .b(4'b0000), .eq(comparator_13_eq));  // open: gt, lt
  and and_7 (and_7_out, comparator_7_eq, and_1_out);
  and and_8 (and_8_out, comparator_9_eq, and_2_out);
  and and_9 (and_9_out, comparator_11_eq, and_3_out);
  Comparator #(.width(4)) comparator_14 (.a(SR_2), .b(4'b0000), .eq(comparator_14_eq));  // open: gt, lt
  and and_10 (and_10_out, comparator_1_eq, and_4_out);
  and and_11 (and_11_out, comparator_3_eq, and_5_out);
  and and_12 (and_12_out, comparator_5_eq, and_6_out);
  and and_13 (and_13_out, ~and_7_out, ~and_8_out, ~and_9_out);  // AND_Gate
  and and_14 (and_14_out, ~and_10_out, ~and_11_out, ~and_12_out);  // AND_Gate
  or or_1 (or_1_out, and_14_out, comparator_13_eq);
  or or_2 (or_2_out, and_13_out, comparator_14_eq);
  Priority_Encoder #(.select(2)) priority_encoder_1 (
    .in0(and_7_out), .in1(and_8_out), .in2(and_9_out), .in3(or_2_out), .out(priority_encoder_1_out),
    .en_in(1'b1));  // open: gs, en_out
  Priority_Encoder #(.select(2)) priority_encoder_2 (
    .in0(and_10_out), .in1(and_11_out), .in2(and_12_out), .in3(or_1_out), .out(priority_encoder_2_out),
    .en_in(1'b1));  // open: gs, en_out
  and and_15 (SHOULD_STALL, LD_IN_EX, or_3_out);
  or or_3 (or_3_out, and_12_out, and_9_out);
  Multiplexer #(.select(2), .width(32), .enable("false")) multiplexer_1 (
    .in0(WB_RES), .in1(MEM_RES), .in2(EX_RES), .in3(VAL_2), .out(VAL_2_2), .sel(priority_encoder_1_out));
  Multiplexer #(.select(2), .width(32), .enable("false")) multiplexer_2 (
    .in0(WB_RES), .in1(MEM_RES), .in2(EX_RES), .in3(VAL_1), .out(VAL_1_2), .sel(priority_encoder_2_out));
endmodule

module CNT_SIG_CONVERT (
  input  [31:0] CNT_SIG,
  input  [3:0] RX,
  input  [3:0] RY,
  input  [3:0] RZ,
  output JMP,
  output HALT,
  output STALL,
  output CHK_Z,
  output READ_MEM,
  output WR_MEM,
  output OFF_TO_ALU,
  output WR_REG,
  output [1:0] ALU_FUNC,
  output [3:0] SR_1,
  output [3:0] SR_2,
  output [3:0] DST
);

  Multiplexer #(.select(2), .width(4), .enable("false")) multiplexer_1 (
    .in0(4'b0000), .in1(RX), .in2(RY), .in3(RZ), .out(SR_1), .sel(CNT_SIG[29:28]));
  Multiplexer #(.select(2), .width(4), .enable("false")) multiplexer_2 (
    .in0(4'b0000), .in1(RX), .in2(RY), .in3(RZ), .out(SR_2), .sel(CNT_SIG[31:30]));
  Multiplexer #(.select(2), .width(4), .enable("false")) multiplexer_3 (
    .in0(4'b0000), .in1(RX), .in2(RY), .in3(RZ), .out(DST), .sel(CNT_SIG[24:23]));

  assign ALU_FUNC = CNT_SIG[27:26];
  assign CHK_Z = CNT_SIG[19];
  assign HALT = CNT_SIG[17];
  assign JMP = CNT_SIG[16];
  assign OFF_TO_ALU = CNT_SIG[22];
  assign READ_MEM = CNT_SIG[20];
  assign STALL = CNT_SIG[18];
  assign WR_MEM = CNT_SIG[21];
  assign WR_REG = CNT_SIG[25];

  // Other names for the same wires on the sheet: DST_SEL[1:0] = CNT_SIG[24:23]; SR_1_SEL[1:0] = CNT_SIG[29:28];
  //   SR_2_SEL[1:0] = CNT_SIG[31:30]
endmodule
